# Fritzing sketch SQVehicleAlarm (saved by Fritzing 0.9.2b)
circuit board: 6.3cm x 6.8cm
breadboards: 1

parts:
  C4 = Capacitor Polarized [package=cpol-radial-10uf-25v]
  C5 = Capacitor Polarized [package=cpol-radial-10uf-25v]
  LED = LED - 3mm [color="Red (633nm)" package="3 mm [THT]"]
  IC2 = ULN2003A [package="DIP16 [THT]"]
  RFduino1 = RFduino
  C7 = Ceramic Capacitor [capacitance=2.2µF package="100 mil [THT, multilayer]"]
  C8 = Ceramic Capacitor [capacitance=2.2µF package="100 mil [THT, multilayer]"]
  RGB_LED = RGB LED - (4 legs) [package="5 mm [THT]"]
  Ignition_Relay = RELAY-2 [package=relay-g5v]
  Interior_Light = female pin header, 4 pins [form="♀ (female)"]
  R2 = Resistor [tolerance=±5% resistance=220 package=THT]
  U2 = Voltage Regulator - 3.3V [package="TO220 [THT]"]
  XTAL1 = Crystal [frequency="16 Mhz" package=THT]
  U1 = atmega328 [package=dip]
  R3 = Resistor [tolerance=±5% resistance=220 package="0603 [SMD]"]
  Relay_&_LED = Header 6 [package=1x06-smd]
  Connect_Relay_&_LED = Header 6 [package=1x06-smd]

nets:
  12V: C4.+, Interior_Light.pin2, U2.input_voltage, Relay_&_LED.2
  GND: C4.-, C5.-, LED.cathode, IC2.0V, RFduino1.gnd, C7.1, C8.1, Interior_Light.pin1, U2.GND, U1.GND, Relay_&_LED.1
  3.3V: C5.+, RFduino1.vin, U2.output_voltage, U1.VCC, U1.AVCC, U1.AREF
  N1: LED.anode, R3.Pin_0
  N2: IC2.In_1, IC2.In_2, IC2.In_3, U1.D6_(PWM)
  N3: IC2.In_6, Interior_Light.pin4
  N4: IC2.In_7, Interior_Light.pin3
  N5: IC2.Out_7, U1.D8
  N6: IC2.Out_6, U1.D7
  N7: IC2.Out_3, IC2.Out_2, IC2.Out_1, Relay_&_LED.6
  N8: RFduino1.gpio4, U1.D2
  N9: RFduino1.gpio5, U1.A5
  N10: RFduino1.gpio6, U1.A4
  N11: C7.0, XTAL1.pin_0, U1.XLAT2
  N12: C8.0, XTAL1.pin_1, U1.XLAT1
  N13: RGB_LED.red_cathode, Connect_Relay_&_LED.2
  N14: RGB_LED.common_anode, R2.Pin_0
  N15: RGB_LED.green_cathode, Connect_Relay_&_LED.3
  N16: RGB_LED.blue_cathode, Connect_Relay_&_LED.4
  N17: Ignition_Relay.2, Connect_Relay_&_LED.5
  N18: Ignition_Relay.9, Connect_Relay_&_LED.1
  N19: R2.Pin_1, Connect_Relay_&_LED.6
  N20: U1.D3_(PWM), R3.Pin_1
  N21: U1.D9_(PWM), Relay_&_LED.3
  N22: U1.D10_(PWM), Relay_&_LED.4
  N23: U1.D11_(PWM), Relay_&_LED.5

notes:
  BT Car Immobiliser  © Bradley Clayton

custom parts:
  RFduino: RFduino board

// code stored in the sketch: SQVehicleAlarm.ino
/* 
* Car Immobiliser Arduino Uno
* The Uno is an I2C Slave
*/
#include <Wire.h>
#include <SQSchedular.h>
#include <SQLED.h>
#include <SQRGBLED.h>

// Pins
int btWakeUpPin = 2;
int onBoardLedPin = 3;
int relayPin = 6;
int ignitionInputPin = 7;
int doorsInputPin = 8;
int ledBluePin = 11;
int ledGreenPin = 10;
int ledRedPin = 9;

// Components
SQLED onBoardLed;
SQRGBLED statusLed;

uint8_t addr = 4;
bool ledOn = false;

void setup() 
{
  pinMode(btWakeUpPin, OUTPUT);
  pinMode(onBoardLedPin, OUTPUT);
  pinMode(relayPin, OUTPUT);
  pinMode(ignitionInputPin, INPUT_PULLUP);
  pinMode(doorsInputPin, INPUT_PULLUP);
  pinMode(ledRedPin, OUTPUT);
  pinMode(ledGreenPin, OUTPUT);
  pinMode(ledBluePin, OUTPUT);
  
  onBoardLed.setup(onBoardLedPin);
  statusLed.setup(ledRedPin, ledGreenPin, ledBluePin);
  
  Wire.begin(4);                // join i2c bus with address #4

  Wire.onReceive(receiveEvent); // register event
  Serial.begin(9600);           // start serial for output
}

void loop() 
{
  onBoardLed.loop();
  statusLed.loop();

  if (!onBoardLed.isFading)
  {
    if (onBoardLed.currentVal() <= 0)
    {
      onBoardLed.fadeToBrightness(255, 3000);
    }
    else
    {
      onBoardLed.fadeToBrightness(0, 3000);
    }
  }

  // Is the status LED already in transitioning to a new colour?
  if (!statusLed.isFading())
  {
      
    // If the status Led is on, fade it to off.
    if (statusLed.currentAverageVal() > 0)
    {
      statusLed.colour(0, 0, 0, 500);
    }
    else if (isIgnitionOn())
    {
      // Fade to green, not too bright.
      statusLed.colour(0, 32, 0, 3000);
    }
    else if (isDoorOpen())
    {
      // Fade to blue.
      statusLed.colour(0, 0, 255, 1000);
    }
    else
    {
      // Fade to red.
      statusLed.colour(255, 0, 0, 1000);
    }
  }
  
}


boolean isDoorOpen()
{
  // If high, the doors are closed. If low, a door is open.
  return !digitalRead(doorsInputPin);
}

boolean isIgnitionOn()
{
  // If low the ignition is on. If high the ignition is off.
  return !digitalRead(ignitionInputPin);
}

// function that executes whenever data is received from master
// this function is registered as an event, see setup()
void receiveEvent(int howMany)
{
  if (Wire.available() && ledOn)
  {
    digitalWrite(3, LOW);
    ledOn = false;
  }
  else if (Wire.available() && !ledOn)
  {
    digitalWrite(3, HIGH);
    ledOn = true;
  }
    
  while(Wire.available() > 0) // loop through all but the last
  {
    char c = Wire.read(); // receive byte as a character
    Serial.print(c);         // print the character
  }
}
